# Fritzing sketch LightGun_v6 (saved by Fritzing 0.9.3b)
circuit board: 10cm x 4cm
breadboards: 2

parts:
  Arduino = Arduino Nano (Rev3.0)
  MP3 = DFRobot DFPlayer Mini [part_number=DFR0299]
  NRF24L01 = NRF24L01+ Breakout Board
  I2C = Header 4 [package=molex-1x4_lock]
  R6 = Resistor [tolerance=±5% resistance=1k package=THT]
  R5 = Resistor [tolerance=±5% resistance=1k package=THT]
  R3 = Resistor [tolerance=±5% resistance=220 package=THT]
  R9 = Resistor [tolerance=±5% resistance=1k package=THT]
  R10 = Resistor [tolerance=±5% resistance=1k package=THT]
  R11 = Resistor [tolerance=±5% resistance=1k package=THT]
  R12 = Resistor [tolerance=±5% resistance=220 package=THT]
  R13 = Resistor [tolerance=±5% resistance=220 package=THT]
  IRRCV1 = female pin header, 3 pins [form="♀ (female)"]
  IRRCV2 = female pin header, 3 pins [form="♀ (female)"]
  ERR = LED - 5mm [color="Red (633nm)" package="5 mm [THT]"]
  TX = LED - 5mm [color="Green (555nm)" package="5 mm [THT]"]
  RX = LED - 5mm [color="Orange (620nm)" package="5 mm [THT]"]
  SPK = female pin header, 2 pins [form="♀ (female)"]
  BATT = female pin header, 2 pins [form="♀ (female)"]
  SHLD = female pin header, 2 pins [form="♀ (female)"]
  LASER = female pin header, 2 pins [form="♀ (female)"]
  R14 = Resistor [tolerance=±5% resistance=100k package=THT]
  R15 = Resistor [tolerance=±5% resistance=100k package=THT]
  IRTX = female pin header, 2 pins [form="♀ (female)"]
  Q5 = TRANSISTOR_NPN [package=to-92]
  Q6 = TRANSISTOR_NPN [package=to-92]
  Q7 = TRANSISTOR_NPN [package=to-92]
  BUZ = Buzzer 12mm [package=buzzer-12mm-ns]
  BTN1 = Header 2 [package=molex-1x2_lock]
  BTN2 = Header 2 [package=molex-1x2_lock]

nets:
  GND: Arduino.GND, MP3.GND-1, MP3.GND-2, NRF24L01.GND, I2C.1, IRRCV1.pin1, IRRCV2.pin1, ERR.anode, TX.anode, RX.anode, BATT.pin1, SHLD.pin1, LASER.pin1, R14.Pin_1, R15.Pin_1, IRTX.pin2, BUZ.1
  N1: Arduino.D2, MP3.RX, BUZ.2
  N2: Arduino.D3, R5.Pin_0
  N3: Arduino.D4, R12.Pin_1
  N4: Arduino.D5, R3.Pin_1
  N5: Arduino.D6, R13.Pin_1
  N6: Arduino.D7, IRRCV1.pin3
  N7: Arduino.D8, IRRCV2.pin3
  N8: Arduino.D9, NRF24L01.CE
  N9: Arduino.D10, NRF24L01.CS
  N10: Arduino.D11/MOSI, NRF24L01.MOSI
  N11: Arduino.D12/MISO, NRF24L01.MISO
  N12: Arduino.VIN, BATT.pin2
  5V: Arduino.5V, MP3.VCC, I2C.2, IRRCV1.pin2, IRRCV2.pin2, Q6.E, Q7.E, BTN1.1, BTN2.1
  N13: Arduino.A5, I2C.4
  N14: Arduino.A4, I2C.3
  N15: Arduino.A3, R9.Pin_0
  N16: Arduino.A2, R6.Pin_0
  N17: Arduino.A1, R11.Pin_0, R14.Pin_0
  N18: Arduino.A0, R10.Pin_0, R15.Pin_0
  3V3: Arduino.3V3, NRF24L01.VCC, Q5.E
  N19: Arduino.D13/SCK, NRF24L01.SCK
  N20: MP3.SPK_1, SPK.pin1
  N21: MP3.SPK_2, SPK.pin2
  N22: R6.Pin_1, Q6.B
  N23: R5.Pin_1, Q5.B
  N24: R3.Pin_0, RX.cathode
  N25: R9.Pin_1, Q7.B
  N26: R10.Pin_1, BTN2.2
  N27: R11.Pin_1, BTN1.2
  N28: R12.Pin_0, ERR.cathode
  N29: R13.Pin_0, TX.cathode
  N30: SHLD.pin2, Q6.C
  N31: LASER.pin2, Q7.C
  N32: IRTX.pin1, Q5.C

notes:
  Lightgun
  gnd
  vcc
  sda
  scl
  v1.1
